# Fritzing sketch ProjetoCarroRoboWifi (saved by Fritzing 0.9.4)
breadboards: 1

parts:
  U1 = NodeMCU V3.0
  L298N1 = L298N DC motor driver
  M1 = DC Motor  # not connected
  M2 = DC Motor  # not connected
  VCC1 = 4 x AAA Battery Mount  # not connected

nets:
  N1: U1.D3, L298N1.IN4
  N2: U1.D4, L298N1.IN3
  N3: U1.GND#6, U1.GND#13, U1.GND#16, U1.GND#33
  N4: U1.D5, L298N1.ENA
  N5: U1.D6, L298N1.ENB
  N6: U1.D7, L298N1.IN2
  N7: U1.D8, L298N1.IN1
  N8: U1.GND#41, L298N1.GND
  N9: U1.A0, L298N1.5V

custom parts:
  NodeMCU V3.0: ESP8266 based NodeMCU
  L298N DC motor driver: 2x DC motor driver with 78M05 positive voltage regulator (7..35 V) L298N: max 46 V, 2 A Set 5 V Enable jumper to enable 5 V regultor (needed for the L298N) and +5 V output at screw terminal or supply external +5 V at screw terminal Set ENA and/or ENB to +5 V to enable motor permanently or supply ENA and/or ENB with PWM signal IN1 and IN2 set rotation directory for motor A (OUT1/OUT2) IN2 and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
